// Digital circuit halfAdder.dig as structural Verilog
module halfAdder (
  input  i_A,
  input  i_B,
  output o_Cout,
  output o_S
);

  wire nand_1_out, nand_2_out, nand_3_out;

  and and_1 (o_Cout, i_A, i_B);
  nand nand_1 (nand_1_out, i_A, i_B);
  nand nand_2 (nand_2_out, i_A, nand_1_out);
  nand nand_3 (nand_3_out, nand_1_out, i_B);
  nand nand_4 (o_S, nand_2_out, nand_3_out);
endmodule

/* Test case Tests:
i_A i_B o_S o_Cout
0 0 0 0 
0 1 1 0
1 0 1 0
1 1 0 1
*/
